# Fritzing sketch beep2 (saved by Fritzing 0.9.8b)
breadboards: 1

parts:
  Raspberry_Pi_1 = Raspberry Pi 3 [part_number=RPI-3-V1.2]
  S1 = Pushbutton [package="[THT]"]
  Q1 = NPN-Transistor [package="TO92 [THT]"]
  C1 = Electrolytic Capacitor [capacitance=10µF voltage=50V package="200 mil [THT, electrolytic]"]
  R1 = Resistor [tolerance=±1% resistance=5100 power=0.25 package=THT]
  R2 = Resistor [tolerance=±1% power=0.25 resistance=200 package=THT]
  LED1 = smd LED [color="Red (633nm)" package="1206 [SMD]"]
  R3 = Resistor [tolerance=±1% power=0.25 resistance=5100 package=THT]
  C3 = Capacitor [part_number="It's actually an orange one" package=cap-pth-5mm]
  C4 = Capacitor [part_number="It's actually an orange one" package=cap-pth-5mm]
  C5 = Capacitor [part_number="It's actually an orange one" package=cap-pth-5mm]
  C6 = Capacitor [part_number="It's actually an orange one" package=cap-pth-5mm]
  C7 = Capacitor [part_number="It's actually an orange one" package=cap-pth-5mm]
  LED2 = smd LED [color="Red (633nm)" package="1206 [SMD]"]
  LED3 = smd LED [color="Red (633nm)" package="1206 [SMD]"]
  LED4 = smd LED [color="Red (633nm)" package="1206 [SMD]"]
  LED5 = smd LED [color="Red (633nm)" package="1206 [SMD]"]

nets:
  N1: Raspberry_Pi_1.3v3, R1.Pin_0
  N2: Raspberry_Pi_1.GPIO3, Q1.B
  N3: Raspberry_Pi_1.GPIO15, S1.Pin_1, S1.Pin_2
  N4: Raspberry_Pi_1.GND, Q1.E
  N5: Raspberry_Pi_1.5V, C1.+, R2.Pin_1, R3.Pin_1, C3.1, C4.1, C5.1, C6.1
  N6: S1.Pin_3, S1.Pin_4, R1.Pin_1
  N7: Q1.C, C1.-, LED1.cathode, C3.2, C4.2, C5.2, C6.2, C7.2, LED2.anode, LED3.anode, LED4.anode, LED5.anode
  N8: R2.Pin_0, C7.1, LED2.cathode, LED3.cathode, LED4.cathode, LED5.cathode
  N9: LED1.anode, R3.Pin_0

notes:
  <- I'm not sure if it's 100Ω or 200Ω.
